# Fritzing sketch TPA6139A2-2out-hpa (saved by Fritzing 0.9.2b)
breadboards: 1

parts:
  U1 = mystery part, 14 pins [chip_label=TPA6139A2]
  U2 = mystery part, 14 pins [chip_label=TPA6139A2]
  C1 = Ceramic Capacitor [capacitance=100nF package="100 mil [THT, multilayer]"]
  C2 = Ceramic Capacitor [capacitance=100nF package="100 mil [THT, multilayer]"]
  J1 = female pin header, 1 pin [form="♀ (female)"]
  J2 = female pin header, 1 pin [form="♀ (female)"]
  C3 = Ceramic Capacitor [capacitance=100nF package="100 mil [THT, multilayer]"]
  C4 = Ceramic Capacitor [capacitance=100nF package="100 mil [THT, multilayer]"]
  J3 = female pin header, 1 pin [form="♀ (female)"]
  J4 = female pin header, 1 pin [form="♀ (female)"]
  C5 = Ceramic Capacitor [capacitance=100nF package="100 mil [THT, multilayer]"]
  J5 = female pin header, 1 pin [form="♀ (female)"]
  J6 = female pin header, 1 pin [form="♀ (female)"]
  C6 = Ceramic Capacitor [capacitance=100nF package="100 mil [THT, multilayer]"]
  C7 = Ceramic Capacitor [capacitance=100nF package="100 mil [THT, multilayer]"]
  C8 = Ceramic Capacitor [capacitance=100nF package="100 mil [THT, multilayer]"]
  R1 = Resistor [tolerance=±5% resistance=47k package=THT]
  R2 = Resistor [tolerance=±5% resistance=47k package=THT]

nets:
  N1: U1.pin1, U2.pin2, J4.pin1
  N2: U1.pin2, J6.pin1
  N3: U1.pin3, U1.pin11, U2.pin3, U2.pin11, C3.0, C5.1, C6.0, C7.1, R1.Pin_0, R2.Pin_0
  N4: U1.pin4, U1.pin10, U2.pin4, U2.pin10, C3.1, C6.1
  N5: U1.pin5, C7.0
  N6: U1.pin6, C8.0
  N7: U1.pin9, C8.1
  N8: U1.pin12, R1.Pin_1
  N9: U1.pin13, J5.pin1
  N10: U1.pin14, U2.pin13, J3.pin1
  N11: U2.pin1, C2.1
  N12: U2.pin5, C5.0
  N13: U2.pin6, C4.0
  N14: U2.pin9, C4.1
  N15: U2.pin12, R2.Pin_1
  N16: U2.pin14, C1.1
  N17: C1.0, J2.pin1
  N18: C2.0, J1.pin1

notes:
  GND
  3.3V
