# Fritzing sketch TPA6139A2ケース内配線 (saved by Fritzing 0.9.2b)
perfboards: 1

parts:
  J1 = female pin header, 3 pins [form="♀ (female)"]
  J2 = female pin header, 3 pins [form="♀ (female)"]
  J3 = female pin header, 3 pins [form="♀ (female)"]
  J4 = female pin header, 2 pins [form="♀ (female)"]
  TRS1 = Audio Jack (TRS) 3.5mm [package="4Ucon 08780 [THT]"]
  TRS2 = Audio Jack (TRS) 3.5mm [package="4Ucon 08780 [THT]"]
  R1 = Rotary Potentiometer (Small) [maximum_resistance=100kΩ package=THT]
  R2 = Rotary Potentiometer (Small) [maximum_resistance=100kΩ package=THT]
  TRS3 = Audio Jack (TRS) 3.5mm [package="4Ucon 08780 [THT]"]
  J5 = Power Jack [package=power_jack_pth]
  S1 = Toggle Switch [package=THT]

nets:
  N1: J1.pin2, R1.leg1, R2.leg1, TRS3.Sleeve
  N2: J1.pin3, R1.wiper
  N3: J2.pin1, TRS1.Sleeve
  N4: J2.pin2, TRS1.Tip
  N5: J2.pin3, TRS1.Ring
  N6: J3.pin1, TRS2.Ring
  N7: J3.pin2, TRS2.Tip
  N8: J3.pin3, TRS2.Sleeve
  N9: J4.pin1, J5.GNDBREAK
  N10: J4.pin2, S1.COM
  N11: R1.leg2, TRS3.Ring
  N12: R2.leg2, TRS3.Tip
  N13: J5.GND, S1.L1
